# Fritzing sketch TuanMinhNguyen (saved by Fritzing 0.9.3b)
circuit board: 8.46667cm x 5.64444cm
breadboards: 1

parts:
  hc-sr1 = hc-sr04
  LED1 = smd LED [color="Red (633nm)" package="1206 [SMD]"]
  LED2 = LED - 5mm [color="Red (633nm)" package="5 mm [THT]"]
  Part1 = Arduino Uno (Rev3) - ICSP

nets (from the pcb view):
  VCC: hc-sr1.VCC, Part1.5V
  N1: hc-sr1.Trig, hc-sr1.Echo, Part1.D11_PWM/MOSI, Part1.D12/MISO
  GND: hc-sr1.GND, LED1.cathode, LED2.cathode, Part1.GND
  N2: LED1.anode, Part1.D13/SCK
  N3: LED2.anode, Part1.D3_PWM
